# Fritzing sketch polaczenie1 (saved by Fritzing 0.9.3b)
breadboards: 1

parts:
  Part1 = Arduino Uno (Rev3)
  Part2 = RFID-RC522 [part_number=101218]
  LED1 = RGB LED (com. cathode, rgb) [package="5 mm [THT]"]
  LED2 = LED - 5mm [color="Red (633nm)" package="5 mm [THT]"]
  R1 = Resistor [tolerance=±5% resistance=220 package=THT]
  R2 = Resistor [tolerance=±5% resistance=220 package=THT]
  R3 = Resistor [tolerance=±5% resistance=220 package=THT]
  Power_plug1 = Power plug

nets:
  N1: Part1.D8, R3.Pin_1
  N2: Part1.D9_PWM, Part2.RST
  N3: Part1.D10_PWM/SS, Part2.SDA
  N4: Part1.D11_PWM/MOSI, Part2.MOSI
  N5: Part1.D12/MISO, Part2.MISO
  N6: Part1.D13/SCK, Part2.SCK
  N7: Part1.D6_PWM, R1.Pin_1
  N8: Part1.D7, R2.Pin_1
  3V3: Part1.3V3, Part2.3.3V
  GND: Part1.GND, Part2.GND, LED1.common_cathode, LED2.cathode, Power_plug1.GND
  VIN: Part1.VIN, Power_plug1.VCC
  N9: LED1.red_anode, R2.Pin_0
  N10: LED1.green_anode, R1.Pin_0
  N11: LED2.anode, R3.Pin_0
