# Fritzing sketch polaczenie3 (saved by Fritzing 0.9.3b)

parts:
  L1 = Solenoid
  Part1 = KY-019 5V Relay Module [package="Breakout board"]

nets:
  N1: L1.pin2, Part1.Common

custom parts:
  KY-019 5V Relay Module: KY-019 5V Relay module, used to control AC circuits.
